// Logisim project d8421+6.circ as structural Verilog: 2 circuits, main circuit main
module main (
  input  [3:0] in_1,
  output [3:0] out_2
);

  wire and_1_out, and_2_out, and_3_out, and_4_out, and_5_out, and_6_out, and_7_out, and_8_out, and_9_out,
       not_1_out, not_2_out, not_3_out, not_4_out;

  not not_1 (not_1_out, in_1[0]);
  not not_2 (not_2_out, in_1[1]);
  not not_3 (not_3_out, in_1[2]);
  not not_4 (not_4_out, in_1[3]);
  and and_1 (and_1_out, not_3_out, not_2_out, in_1[0]);
  and and_2 (and_2_out, not_4_out, in_1[0]);
  and and_3 (and_3_out, not_2_out, not_3_out);
  and and_4 (and_4_out, not_2_out, not_4_out);
  and and_5 (and_5_out, not_4_out, in_1[2], in_1[1]);
  and and_6 (and_6_out, not_3_out, not_2_out);
  and and_7 (and_7_out, in_1[1], not_4_out);
  and and_8 (and_8_out, in_1[2], not_4_out);
  and and_9 (and_9_out, in_1[3], not_2_out, not_3_out);
  or or_1 (out_2[0], and_1_out, and_2_out);
  or or_2 (out_2[1], and_3_out, and_4_out);
  or or_3 (out_2[2], and_5_out, and_6_out);
  or or_4 (out_2[3], and_7_out, and_8_out, and_9_out);
endmodule

module D (
  input  [3:0] Q,
  output [4:0] Y
);

  wire and_1_out, and_2_out, and_3_out, and_4_out, and_5_out, not_1_out, not_2_out, not_3_out, or_1_out;

  or or_1 (or_1_out, Q[0], Q[1]);
  not not_1 (not_1_out, Q[0]);
  not not_2 (not_2_out, Q[1]);
  not not_3 (not_3_out, Q[3]);
  and and_1 (and_1_out, or_1_out, Q[3]);
  or or_2 (Y[4], and_1_out, Q[3]);
  and and_2 (and_2_out, Q[0], Q[1]);
  and and_3 (and_3_out, Q[0], Q[3]);
  and and_4 (and_4_out, not_1_out, not_2_out);
  and and_5 (and_5_out, not_1_out, not_3_out);
  xor xor_1 (Y[0], Q[0], Q[1]);
  or or_3 (Y[3], and_2_out, and_3_out);
  or or_4 (Y[2], and_4_out, and_5_out);

  assign Q[2] = Q[3];
  assign Y[1] = Y[2];
endmodule
