// Logisim project ОДЗ сднф.circ as structural Verilog: 2 circuits, main circuit main
module main (
  input  A,
  input  B,
  input  C,
  input  A_2,
  input  B_2,
  input  C_2,
  output S,
  output P,
  output S_2,
  output P_2
);

  wire and_1_out, and_2_out, and_3_out, and_4_out, and_5_out, and_6_out, and_7_out, and_8_out, and_9_out,
       and_10_out, and_11_out, and_12_out, and_13_out, and_14_out, and_15_out, and_16_out, not_1_out,
       not_2_out, not_3_out, not_4_out, not_5_out, not_6_out;

  not not_1 (not_1_out, A_2);
  not not_2 (not_2_out, B_2);
  not not_3 (not_3_out, C_2);
  and and_1 (and_1_out, not_1_out, not_2_out, C_2);
  and and_2 (and_2_out, not_1_out, B_2, not_3_out);
  and and_3 (and_3_out, A_2, not_2_out, not_3_out);
  and and_4 (and_4_out, A_2, B_2, C_2);
  and and_5 (and_5_out, not_1_out, B_2, C_2);
  and and_6 (and_6_out, A_2, not_2_out, C_2);
  and and_7 (and_7_out, A_2, B_2, not_3_out);
  and and_8 (and_8_out, A_2, B_2, C_2);
  or or_1 (S_2, and_1_out, and_2_out, and_3_out, and_4_out);
  or or_2 (P_2, and_5_out, and_6_out, and_7_out, and_8_out);
  not not_4 (not_4_out, A);
  not not_5 (not_5_out, B);
  not not_6 (not_6_out, C);
  and and_9 (and_9_out, not_4_out, C, not_5_out);
  and and_10 (and_10_out, not_4_out, B, not_6_out);
  and and_11 (and_11_out, A, not_5_out, not_6_out);
  and and_12 (and_12_out, A, B, C);
  and and_13 (and_13_out, not_4_out, B, C);
  and and_14 (and_14_out, A, not_5_out, C);
  and and_15 (and_15_out, A, B, not_6_out);
  and and_16 (and_16_out, A, B, C);
  or or_3 (S, and_9_out, and_10_out, and_11_out, and_12_out);
  or or_4 (P, and_13_out, and_14_out, and_15_out, and_16_out);

  // Notes on the sheet:
  //   A B P   !A !B !P
endmodule

module D (
  input  [3:0] Q,
  output [4:0] Y
);

  wire and_1_out, and_2_out, and_3_out, and_4_out, and_5_out, not_1_out, not_2_out, not_3_out, or_1_out;

  or or_1 (or_1_out, Q[0], Q[1]);
  not not_1 (not_1_out, Q[0]);
  not not_2 (not_2_out, Q[1]);
  not not_3 (not_3_out, Q[3]);
  and and_1 (and_1_out, or_1_out, Q[3]);
  or or_2 (Y[4], and_1_out, Q[3]);
  and and_2 (and_2_out, Q[0], Q[1]);
  and and_3 (and_3_out, Q[0], Q[3]);
  and and_4 (and_4_out, not_1_out, not_2_out);
  and and_5 (and_5_out, not_1_out, not_3_out);
  xor xor_1 (Y[0], Q[0], Q[1]);
  or or_3 (Y[3], and_2_out, and_3_out);
  or or_4 (Y[2], and_4_out, and_5_out);

  assign Q[2] = Q[3];
  assign Y[1] = Y[2];
endmodule
