// Logisim project счётчик вычит..circ as structural Verilog: 1 circuit, main circuit main
module main (
  input  V
);

  wire and_1_out, and_2_out, and_3_out, clock_1_out, nq1_out, nq2_out;
  wire [2:0] t_ff_3_q;

  not nq2 (nq2_out, t_ff_3_q[1]);
  not nq1 (nq1_out, t_ff_3_q[0]);
  and and_1 (and_1_out, nq2_out, V, nq1_out);
  and and_2 (and_2_out, V, nq1_out);
  buf and_3 (and_3_out, V);  // AND_Gate
  Clock clock_1 (.out(clock_1_out));
  T_Flip_Flop t_ff_1 (.clk(clock_1_out), .T(and_1_out), .Q(t_ff_3_q[2]));  // open: Qn, preset, reset, en
  T_Flip_Flop t_ff_2 (.clk(clock_1_out), .T(and_2_out), .Q(t_ff_3_q[1]));  // open: Qn, preset, reset, en
  T_Flip_Flop t_ff_3 (.clk(clock_1_out), .T(and_3_out), .Q(t_ff_3_q[0]));  // open: Qn, preset, reset, en
  // Probe on t_ff_3_q
  Clock clock_2 ();  // open: out
  // AND_Gate and_4 is placed but not wired

  // Notes on the sheet:
  //   q2
  //   q3
  //   q1
  //   v
endmodule
